# Fritzing sketch cablage (saved by Fritzing 0.9.3b)
breadboards: 1

parts:
  U1 = ESP32-38PinWide [part_number=ESP32-38PinWide]
  R1 = Resistor [tolerance=±5% resistance=220 package=THT]
  D1 = LED_BARGRAPH_10 [package=led_bargaph_10]
  R2 = Resistor [tolerance=±20% resistance=220 package="0603 [SMD]"]
  R3 = Resistor [tolerance=±5% resistance=220 package=THT]
  R4 = Resistor [tolerance=±20% resistance=220 package="0603 [SMD]"]
  R5 = Resistor [tolerance=±20% resistance=220 package="0603 [SMD]"]
  R6 = Resistor [tolerance=±20% resistance=220 package="0603 [SMD]"]
  R7 = PHOTOCELL [package=photocell-kit]
  R8 = Resistor [tolerance=±20% resistance=220 package=THT]
  R9 = Resistor [tolerance=±20% resistance=220 package="0603 [SMD]"]
  R10 = Resistor [tolerance=±20% resistance=220 package="0603 [SMD]"]
  R11 = Resistor [tolerance=±20% resistance=220 package="0603 [SMD]"]
  R12 = Resistor [tolerance=±20% resistance=220 package="0603 [SMD]"]
  R13 = Rotary Potentiometer (Large) [maximum_resistance=100kΩ package=THT]
  DHT1 = Humidity and Temperature Sensor DHT11
  Composant1 = LCD1602-I2C

nets:
  N1: U1.3.3, R13.leg2
  N2: U1.GPIO34, R13.wiper
  N3: U1.GPIO35, U1.GPIO32, R11.Pin_0, R11.Pin_1
  N4: U1.GPIO33, U1.GPIO25, D1.C_A, R10.Pin_0, R10.Pin_1, DHT1.Data-signal
  N5: U1.GPIO26, R9.Pin_0, R9.Pin_1
  VCC: U1.VIN, R5.Pin_1, R7.P$2, DHT1.Vcc, Composant1.VCC
  N6: U1.GPIO15, U1.GPIO2, D1.A_A, R12.Pin_0
  N7: U1.GPIO16, R6.Pin_0, R6.Pin_1
  N8: U1.GPIO17, U1.GPIO5, R2.Pin_0, R2.Pin_1
  N9: U1.GPIO18, R1.Pin_1
  GND: U1.GPIO19, U1.GND, D1.I_C, D1.H_C, D1.F_C, D1.A_C, R13.leg1, DHT1.GND_2, Composant1.GND
  N10: U1.GPIO21, Composant1.SDA
  N11: U1.GPIO22, Composant1.SCL
  N12: D1.F_A, R4.Pin_0, DHT1.GND_1
  N13: D1.J_A, R3.Pin_0
  N14: R7.P$1, R8.Pin_0, R8.Pin_1

custom parts:
  ESP32-38PinWide: Generic 38-Pin ESP32 with wide format (only access to one side of pins on a breadboard) based on Stephen Lilley's HiLetgo ESP-WROOM-32 ESP32 ESP-32S Development Board.
  Humidity and Temperature Sensor DHT11: Digital relative humidity & temperature sensor DHT11
  LCD1602-I2C: A standard character display, usually with 2x16 characters. Comes in many colors with LCM1602 IIC attached.
